# Fritzing sketch HexBusSDUno (saved by Fritzing 0.9.3b)
breadboards: 1

parts:
  Part1 = MicroSD Card Module
  Part2 = Arduino Uno (Rev3)
  J1 = female pin header, 10 pins [form="♀ (female)"]
  R1 = Resistor [tolerance=±5% resistance=10k package=THT]
  LED1 = LED - 3mm [color="Yellow (592nm)" package="3 mm [THT]"]
  R2 = Resistor [tolerance=±5% resistance=220 package=THT]

nets:
  GND: Part1.GND, Part2.GND, J1.pin10, R2.Pin_0
  VCC: Part1.VCC, Part2.5V, R1.Pin_1
  N1: Part1.MISO, Part2.D12/MISO
  N2: Part1.MOSI, Part2.D11_PWM/MOSI
  N3: Part1.SCK, Part2.D13/SCK
  N4: Part1.CS, Part2.D10_PWM/SS
  N5: Part2.A0, J1.pin2, J1.pin3
  N6: Part2.A1, J1.pin4
  N7: Part2.A2, J1.pin5
  N8: Part2.A3, J1.pin6
  N9: Part2.D2, LED1.anode
  N10: Part2.D3_PWM, J1.pin7
  N11: Part2.D7, J1.pin8, R1.Pin_0
  N12: LED1.cathode, R2.Pin_1

notes:
  Arduino UNO based version
  10pin header from top to bottom:
  D0-D3, HSK, BAV, GND
